# Fritzing sketch backpack (saved by Fritzing 0.9.2b)

parts:
  Part1 = Arduino Uno (Rev3)
  Part2 = Arduino Nano (Rev3.0)

nets:
  N1: Part1.A4/SDA, Part2.A4
  N2: Part1.A5/SCL, Part2.A5
  5V: Part1.5V, Part2.VIN
  GND: Part1.GND, Part2.GND
